// Logisim project Universal_gates.circ as structural Verilog: 7 circuits, main circuit main
module main (
  input  A,
  input  A_2,
  input  in_3,
  input  in_4,
  input  in_5,
  input  in_6,
  input  in_7,
  input  in_8,
  input  in_9,
  input  in_10,
  input  in_11,
  input  in_12,
  input  in_13,
  input  in_14,
  output A_not,
  output A_not_2,
  output out_17,
  output out_18,
  output out_19,
  output out_20,
  output out_21
);

  wire nand_1_out, nand_2_out, nand_4_out, nand_7_out, nand_8_out, nand_9_out, nand_10_out, nand_11_out,
       nor_1_out, nor_2_out, nor_3_out, nor_7_out, nor_8_out;

  nor nor_1 (nor_1_out, in_5, in_5);
  nor nor_2 (nor_2_out, in_8, in_8);
  nand nand_1 (nand_1_out, in_9, in_9);
  nand nand_2 (nand_2_out, in_10, in_10);
  nor nor_3 (nor_3_out, in_11, in_12);
  nand nand_3 (A_not, A, A);
  nor nor_4 (A_not_2, A_2, A_2);
  nand nand_4 (nand_4_out, in_3, in_4);
  nand nand_5 (out_20, nand_1_out, nand_2_out);
  nor nor_5 (out_21, nor_3_out, nor_3_out);
  nand nand_6 (out_17, nand_4_out, nand_4_out);
  nor nor_6 (out_18, nor_1_out, nor_2_out);
  nand nand_7 (nand_7_out, in_6, in_6);
  nand nand_8 (nand_8_out, in_7, in_7);
  nand nand_9 (nand_9_out, in_6, in_7);
  nand nand_10 (nand_10_out, nand_7_out, nand_8_out);
  nor nor_7 (nor_7_out, in_13, in_14);
  nor nor_8 (nor_8_out, nor_7_out, nor_7_out);
  nand nand_11 (nand_11_out, nand_9_out, nand_10_out);
  // NOR_Gate nor_9 is placed but not wired
  nand nand_12 (out_19, nand_11_out, nand_11_out);

  // Notes on the sheet:
  //   NOT by NAND
  //   NOT by NOR
  //   AND BY NAND
  //   AND BY NOR
  //   OR by NAND
  //   OR by NOR
endmodule

module half_adder (
  input  A,
  input  B,
  output sum,
  output C_out
);

  xor xor_1 (sum, A, B);
  and and_1 (C_out, A, B);
endmodule

module full_adder (
  input  A,
  input  B,
  input  Cin,
  output Sum,
  output C_out
);

  wire and_1_out, and_2_out, xor_1_out;

  xor xor_1 (xor_1_out, A, B);
  and and_1 (and_1_out, A, B);
  and and_2 (and_2_out, xor_1_out, Cin);
  xor xor_2 (Sum, xor_1_out, Cin);
  or or_1 (C_out, and_1_out, and_2_out);
endmodule

module full_adder_by_half_adder (
  input  C_in,
  input  A,
  input  B,
  output Sum,
  output C_out
);

  wire half_adder_1_c_out, half_adder_1_sum, half_adder_2_c_out;

  half_adder half_adder_1 (.A(A), .B(B), .sum(half_adder_1_sum), .C_out(half_adder_1_c_out));
  half_adder half_adder_2 (.A(half_adder_1_sum), .B(C_in), .sum(Sum), .C_out(half_adder_2_c_out));
  or or_1 (C_out, half_adder_2_c_out, half_adder_1_c_out);
endmodule

module Parallel_Adder (
  input  Cin,
  input  [3:0] A,
  input  [3:0] B,
  output S1,
  output S2,
  output S3,
  output S4,
  output carry_out
);

  wire full_adder_by_half_adder_1_c_out, full_adder_by_half_adder_2_c_out, full_adder_by_half_adder_3_c_out;

  full_adder_by_half_adder full_adder_by_half_adder_1 (
    .C_in(Cin), .A(A[0]), .B(B[0]), .Sum(S1), .C_out(full_adder_by_half_adder_1_c_out));
  full_adder_by_half_adder full_adder_by_half_adder_2 (
    .C_in(full_adder_by_half_adder_1_c_out), .A(A[1]), .B(B[1]), .Sum(S2),
    .C_out(full_adder_by_half_adder_2_c_out));
  full_adder_by_half_adder full_adder_by_half_adder_3 (
    .C_in(full_adder_by_half_adder_2_c_out), .A(A[2]), .B(B[2]), .Sum(S3),
    .C_out(full_adder_by_half_adder_3_c_out));
  full_adder_by_half_adder full_adder_by_half_adder_4 (
    .C_in(full_adder_by_half_adder_3_c_out), .A(A[3]), .B(B[3]), .Sum(S4), .C_out(carry_out));
endmodule

module parallel_adder_2_bit (
  input  A0,
  input  A1,
  input  C_in,
  input  B0,
  input  B1,
  output Sum_0,
  output SUM_1,
  output C_out
);

  wire full_adder_1_c_out;

  full_adder full_adder_1 (.A(A0), .B(B0), .Cin(C_in), .Sum(Sum_0), .C_out(full_adder_1_c_out));
  full_adder full_adder_2 (.A(A1), .B(B1), .Cin(full_adder_1_c_out), .Sum(SUM_1), .C_out(C_out));
endmodule

module mult_2_bit (
  input  A1,
  input  A0,
  input  B0,
  input  B1,
  output p3,
  output p2,
  output p1,
  output p0
);

  wire and_1_out, and_2_out, and_3_out;

  and and_1 (and_1_out, B0, A1);
  and and_2 (and_2_out, B1, A1);
  and and_3 (and_3_out, B1, A0);
  parallel_adder_2_bit parallel_adder_2_bit_1 (
    .A0(and_3_out), .A1(and_2_out), .B0(and_1_out), .B1(1'b0), .Sum_0(p1), .SUM_1(p2), .C_out(p3));  // open: C_in
  and and_4 (p0, B0, A0);
endmodule
